# Fritzing sketch PCF8574 (saved by Fritzing 0.9.3b)
breadboards: 2

parts:
  S1 = Momentary Switch [package=ksa_sealed_tac_switch]
  S2 = Momentary Switch [package=ksa_sealed_tac_switch]
  Onderdeel1 = Adafruit T-Cobbler Plus [part_number="Adafruit #1989 and #2028"]
  S3 = Momentary Switch [package=ksa_sealed_tac_switch]
  S4 = Momentary Switch [package=ksa_sealed_tac_switch]
  LED1 = smd LED [color="Green (570nm)" package="1206 [SMD]"]
  LED2 = smd LED [color="Yellow (595nm)" package="1206 [SMD]"]
  LED3 = smd LED [color="Blue (525nm)" package="1206 [SMD]"]
  LED4 = smd LED [color="Red (660nm)" package="1206 [SMD]"]
  R1 = Resistor [tolerance=±5% resistance=220 package="0805 [SMD]"]
  R2 = Resistor [tolerance=±5% resistance=220 package="0805 [SMD]"]
  R3 = Resistor [tolerance=±5% resistance=220 package="0805 [SMD]"]
  R4 = Resistor [tolerance=±5% resistance=220 package="0805 [SMD]"]
  LED5 = smd LED [color="Red (660nm)" package="1206 [SMD]"]
  LED6 = smd LED [color="Blue (525nm)" package="1206 [SMD]"]
  LED7 = smd LED [color="Yellow (595nm)" package="1206 [SMD]"]
  LED8 = smd LED [color="Green (570nm)" package="1206 [SMD]"]
  R5 = Resistor [tolerance=±5% resistance=220 package="0805 [SMD]"]
  R6 = Resistor [tolerance=±5% resistance=220 package="0805 [SMD]"]
  R7 = Resistor [tolerance=±5% resistance=220 package="0805 [SMD]"]
  R8 = Resistor [tolerance=±5% resistance=220 package="0805 [SMD]"]
  S5 = Momentary Switch [package=ksa_sealed_tac_switch]
  S6 = Momentary Switch [package=ksa_sealed_tac_switch]
  S7 = Momentary Switch [package=ksa_sealed_tac_switch]
  S8 = Momentary Switch [package=ksa_sealed_tac_switch]
  U1 = PCF8574 [package="DIP16 [THT]"]
  R9 = Resistor [tolerance=±5% resistance=10k package="0805 [SMD]"]
  R10 = Resistor [tolerance=±5% resistance=10k package="0805 [SMD]"]
  R11 = Resistor [tolerance=±5% resistance=10k package="0805 [SMD]"]
  R12 = Resistor [tolerance=±5% resistance=10k package="0805 [SMD]"]

nets:
  N1: S1.2, S2.2, Onderdeel1.+3.3V_2, S3.2, S4.2
  N2: S1.3, Onderdeel1.GPIO20
  N3: S2.3, Onderdeel1.GPIO21
  +3.3V: Onderdeel1.+3.3V, S5.2, S6.2, S7.2, S8.2, U1.VCC
  N4: Onderdeel1.SDA, U1.SDA
  N5: Onderdeel1.SCL, U1.SCL
  GND: Onderdeel1.GND, LED1.cathode, LED2.cathode, LED3.cathode, LED4.cathode, R5.Pin_1, R6.Pin_1, R7.Pin_1, R8.Pin_1, U1.A0, U1.A1, U1.A3, U1.GND, R9.Pin_1, R10.Pin_1, R11.Pin_1, R12.Pin_1
  N6: Onderdeel1.GPIO6, R1.Pin_1
  N7: Onderdeel1.GPIO13, R4.Pin_1
  N8: Onderdeel1.GPIO19, R3.Pin_1
  N9: Onderdeel1.GPIO26, R2.Pin_1
  N10: Onderdeel1.GPIO18, U1.INT
  N11: Onderdeel1.GPIO12, S4.3
  N12: Onderdeel1.GPIO16, S3.3
  N13: LED1.anode, R3.Pin_0
  N14: LED2.anode, R1.Pin_0
  N15: LED3.anode, R4.Pin_0
  N16: LED4.anode, R2.Pin_0
  N17: LED5.cathode, U1.P0
  N18: LED5.anode, R7.Pin_0
  N19: LED6.cathode, U1.P2
  N20: LED6.anode, R5.Pin_0
  N21: LED7.cathode, U1.P3
  N22: LED7.anode, R8.Pin_0
  N23: LED8.cathode, U1.P1
  N24: LED8.anode, R6.Pin_0
  N25: S5.3, U1.P7
  N26: S5.4, R12.Pin_0
  N27: S6.3, U1.P6
  N28: S6.4, R11.Pin_0
  N29: S7.3, U1.P5
  N30: S7.4, R10.Pin_0
  N31: S8.3, U1.P4
  N32: S8.4, R9.Pin_0

custom parts:
  Adafruit T-Cobbler Plus: The Raspberry Pi has landed on the Maker World like a 40-GPIO pinned, quad-USB ported, credit card sized bomb of DIY joy. And while you can use most of our great Model B accessories by hooking up our downgrade cable, its probably a good time to upgrade your set up and accessorize using all of the 40 pins. That's why we now carry the Assembled Adafruit Pi T-Cobbler Plus - Breakout + Cable for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
