# Fritzing sketch Conveyor (saved by Fritzing 0.9.3b)
breadboards: 2

parts:
  S1 = Momentary Switch [package=ksa_sealed_tac_switch]
  S2 = Momentary Switch [package=ksa_sealed_tac_switch]
  Onderdeel1 = Adafruit T-Cobbler Plus [part_number="Adafruit #1989 and #2028"]
  RE1 = Rotary Encoder [package=THT]
  S3 = Momentary Switch [package=ksa_sealed_tac_switch]
  S4 = Momentary Switch [package=ksa_sealed_tac_switch]
  S5 = Momentary Switch [package=ksa_sealed_tac_switch]
  S6 = Momentary Switch [package=ksa_sealed_tac_switch]
  U1 = POT [package=pot_alpha_rv16af-20]
  IC1 = MCP3008 8-channel 10-bit ADC [part_number=MCP3008]
  LED1 = smd LED [color="Green (570nm)" package="1206 [SMD]"]
  LED2 = smd LED [color="Yellow (595nm)" package="1206 [SMD]"]
  LED3 = smd LED [color="Blue (525nm)" package="1206 [SMD]"]
  LED4 = smd LED [color="Red (660nm)" package="1206 [SMD]"]
  Onderdeel2 = Bluetooth HC-05 Macho  # not connected
  R1 = Resistor [tolerance=±5% resistance=220 package="0805 [SMD]"]
  R2 = Resistor [tolerance=±5% resistance=220 package="0805 [SMD]"]
  R3 = Resistor [tolerance=±5% resistance=220 package="0805 [SMD]"]
  R4 = Resistor [tolerance=±5% resistance=220 package="0805 [SMD]"]
  X1 = X113647 Stepper Driver Board [package=board]
  MOTOR1 = 28BYJ-48 Stepper Motor  # not connected

nets:
  N1: S1.2, S2.2, Onderdeel1.+3.3V, RE1.EncoderPinC, S3.2, S4.2, S5.2, S6.2, U1.A, U1.E, IC1.no_name_yet#15, IC1.no_name_yet#16
  N2: S1.3, Onderdeel1.GPIO24
  N3: S2.3, Onderdeel1.GPIO18
  N4: Onderdeel1.GND, IC1.no_name_yet#9, IC1.no_name_yet#14, R1.Pin_1, R2.Pin_1, R3.Pin_1, R4.Pin_1
  N5: Onderdeel1.GPIO17, X1.IN1
  N6: Onderdeel1.GPIO27, X1.IN2
  N7: Onderdeel1.GPIO22, X1.IN3
  N8: Onderdeel1.MOSI, IC1.no_name_yet#11
  N9: Onderdeel1.MISO, IC1.no_name_yet#12
  N10: Onderdeel1.SCLK, IC1.no_name_yet#13
  N11: Onderdeel1.GPIO5, LED1.cathode
  N12: Onderdeel1.GPIO6, LED2.cathode
  N13: Onderdeel1.GPIO13, LED3.cathode
  N14: Onderdeel1.GPIO19, LED4.cathode
  N15: Onderdeel1.GPIO26, S6.4
  N16: Onderdeel1.+5V, X1.+V
  N17: Onderdeel1.GPIO23, X1.IN4
  N18: Onderdeel1.GPIO25, S3.3
  N19: Onderdeel1.CE1, IC1.no_name_yet#10
  N20: Onderdeel1.GPIO12, S4.3
  N21: Onderdeel1.GPIO16, S5.3
  N22: Onderdeel1.GPIO20, RE1.EncoderPinA
  N23: Onderdeel1.GPIO21, RE1.EncoderPinB
  N24: U1.S, IC1.no_name_yet#1
  N25: LED1.anode, R2.Pin_0
  N26: LED2.anode, R3.Pin_0
  N27: LED3.anode, R4.Pin_0
  N28: LED4.anode, R1.Pin_0

custom parts:
  Adafruit T-Cobbler Plus: The Raspberry Pi has landed on the Maker World like a 40-GPIO pinned, quad-USB ported, credit card sized bomb of DIY joy. And while you can use most of our great Model B accessories by hooking up our downgrade cable, its probably a good time to upgrade your set up and accessorize using all of the 40 pins. That's why we now carry the Assembled Adafruit Pi T-Cobbler Plus - Breakout + Cable for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
  Rotary Encoder: Rotary Encoder from ALPSec11e with switch.
  X113647 Stepper Driver Board: A common stepper motor driver board based on ULN2003APG darlington array
  28BYJ-48 Stepper Motor: 28BYJ-48 gear-reduction stepper motor (small)
