# Fritzing sketch RobotCar (saved by Fritzing 0.9.3b)
breadboards: 2

parts:
  S1 = Momentary Switch [package=ksa_sealed_tac_switch]
  S2 = Momentary Switch [package=ksa_sealed_tac_switch]
  Onderdeel1 = Adafruit T-Cobbler Plus [part_number="Adafruit #1989 and #2028"]
  RE1 = Rotary Encoder [package=THT]
  S3 = Momentary Switch [package=ksa_sealed_tac_switch]
  S4 = Momentary Switch [package=ksa_sealed_tac_switch]
  S5 = Momentary Switch [package=ksa_sealed_tac_switch]
  S6 = Momentary Switch [package=ksa_sealed_tac_switch]
  LED1 = smd LED [color="Green (570nm)" package="1206 [SMD]"]
  LED2 = smd LED [color="Yellow (595nm)" package="1206 [SMD]"]
  LED3 = smd LED [color="Blue (525nm)" package="1206 [SMD]"]
  LED4 = smd LED [color="Red (660nm)" package="1206 [SMD]"]
  Onderdeel2 = Bluetooth HC-05 Macho  # not connected
  R1 = Resistor [tolerance=±5% resistance=220 package="0805 [SMD]"]
  R2 = Resistor [tolerance=±5% resistance=220 package="0805 [SMD]"]
  R3 = Resistor [tolerance=±5% resistance=220 package="0805 [SMD]"]
  R4 = Resistor [tolerance=±5% resistance=220 package="0805 [SMD]"]
  X1 = X113647 Stepper Driver Board [package=board]
  MOTOR1 = 28BYJ-48 Stepper Motor  # not connected
  Grove1 = Grove OLED 128x96

nets:
  +3.3V: S1.2, S2.2, Onderdeel1.+3.3V, RE1.EncoderPinC, S3.2, S4.2, S5.2, S6.2, Grove1.VCC
  N1: S1.4, Onderdeel1.GPIO19
  N2: S2.4, Onderdeel1.GPIO26
  N3: Onderdeel1.SDA, Grove1.SDA
  N4: Onderdeel1.SCL, Grove1.SCL
  GND: Onderdeel1.GND, R1.Pin_1, R2.Pin_1, R3.Pin_1, R4.Pin_1, X1.GND, Grove1.GND
  N5: Onderdeel1.GPIO17, X1.IN4
  N6: Onderdeel1.GPIO27, X1.IN3
  N7: Onderdeel1.GPIO22, X1.IN2
  N8: Onderdeel1.GPIO5, X1.IN1
  N9: Onderdeel1.GPIO6, S5.4
  N10: Onderdeel1.GPIO13, S4.4
  N11: Onderdeel1.+5V, X1.+V
  N12: Onderdeel1.GPIO18, LED1.cathode
  N13: Onderdeel1.GPIO23, LED2.cathode
  N14: Onderdeel1.GPIO24, LED3.cathode
  N15: Onderdeel1.GPIO25, LED4.cathode
  N16: Onderdeel1.GPIO12, RE1.EncoderPinB
  N17: Onderdeel1.GPIO16, RE1.EncoderPinA
  N18: Onderdeel1.GPIO20, S6.3
  N19: Onderdeel1.GPIO21, S5.3
  N20: LED1.anode, R2.Pin_0
  N21: LED2.anode, R3.Pin_0
  N22: LED3.anode, R4.Pin_0
  N23: LED4.anode, R1.Pin_0

custom parts:
  Adafruit T-Cobbler Plus: The Raspberry Pi has landed on the Maker World like a 40-GPIO pinned, quad-USB ported, credit card sized bomb of DIY joy. And while you can use most of our great Model B accessories by hooking up our downgrade cable, its probably a good time to upgrade your set up and accessorize using all of the 40 pins. That's why we now carry the Assembled Adafruit Pi T-Cobbler Plus - Breakout + Cable for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
  Rotary Encoder: Rotary Encoder from ALPSec11e with switch.
  X113647 Stepper Driver Board: A common stepper motor driver board based on ULN2003APG darlington array
  28BYJ-48 Stepper Motor: 28BYJ-48 gear-reduction stepper motor (small)
