# Fritzing sketch LightShowSchema (saved by Fritzing 0.9.3b)
breadboards: 1

parts:
  Raspberry_Pi_1 = Raspberry Pi 3 [part_number=RPI-3-V1.2]
  S1 = Momentary Switch [package=ksa_sealed_tac_switch]
  S2 = Momentary Switch [package=ksa_sealed_tac_switch]
  U1 = 74HC4052 [package=dil16]
  U5 = POT [package=alps_pot]

nets:
  N1: Raspberry_Pi_1.3v3, S1.3, S2.3, U5.E
  N2: Raspberry_Pi_1.GND, U5.A
  N3: U1.Y0, U5.S
